# Fritzing sketch DCMotor (saved by Fritzing 0.9.8b)
breadboards: 1

parts:
  Part1 = Arduino Uno (Rev3)
  IC1 = L293D [package=THT]
  M1 = gear-motor

nets:
  N1: Part1.D10_PWM/SS, IC1.In_2
  N2: Part1.D11_PWM/MOSI, IC1.In_1
  N3: Part1.D12/MISO, IC1.Enable_1
  N4: Part1.5V, IC1.+Vmotor, IC1.+V
  N5: IC1.Out_1_(_Controlled_by_Enable_1_), M1.pin_2
  N6: IC1.Out_2_(_Controlled_by_Enable_1_), M1.pin_1

// code stored in the sketch: dc.ino
/* Oled Display int */
//---------------------------------------------------

#include <Wire.h>
#include <Adafruit_SSD1306.h>
#include <Adafruit_GFX.h>

// OLED display TWI address
#define OLED_ADDR   0x3C

  
// reset pin not used on 4-pin OLED module
Adafruit_SSD1306 display(-1);  // -1 = no reset pin

// 128 x 64 pixel display
#if (SSD1306_LCDHEIGHT != 64)
#error("Height incorrect, please fix Adafruit_SSD1306.h!");
#endif
//---------------------------------------------------



// initialize Dc motor pins 
//---------------------------------------------------
int in1 = 9; // used for control too 
int in2 = 10;
int inspeed = 11;



int butt = 7; // button 
int red = 2; //led 1
int yellow = 3; // led 2

int in1state = LOW; //in1 state update
int in2state = HIGH; //in2 state update
unsigned long potvalue = map(analogRead(A0), 0, 1023, 60000 ,900000);
unsigned long previousMillis = potvalue;        // update millis

int buttonState = 0;         // current state of the button



 
void setup() 
{
 // initialize Dc motor pins
  pinMode(in1, OUTPUT);
  pinMode(in2, OUTPUT);
  pinMode(inspeed, OUTPUT);  
  pinMode(butt, OUTPUT);   //button
  pinMode(red, OUTPUT);
  pinMode(yellow, OUTPUT);



  
  // initialize and clear display
  //---------------------------------------------------
  display.begin(SSD1306_SWITCHCAPVCC, OLED_ADDR);
  display.clearDisplay();
  display.display();
  // display a line of text
  display.setTextSize(1.5);
  display.setTextColor(WHITE);
  display.setCursor(0,10);
  display.print("Sam Fishing");
    display.setTextSize(2);
  display.setCursor(0,25);
  display.print("><(((('>");

  
  // update display with all of the above graphics
  display.display();
  // Small delay before clearing the display 
  delay(1000);
  display.clearDisplay();
}



void loop()
{
    buttonState = digitalRead(butt);

  //Display 
  //---------------------------------------------------
  unsigned long podisplay = (map(analogRead(A0), 0, 1023, 60000 ,900000)/60000);
  display.clearDisplay();
  display.setTextSize(1.5);
  display.setTextColor(WHITE);
  display.setCursor(10,10);
  display.print("Round Time");

  display.setTextSize(2);
  display.setTextColor(WHITE);
  display.setCursor(10,30);
  display.print(podisplay);

  display.setTextSize(1);
  display.setTextColor(WHITE);
  display.setCursor(60,50);
  display.print("Mints");
  
  // update display with all of the above graphics
  display.display();
  delay(1);        // delay in between reads for stability


if (buttonState == LOW) {
 //Set the speed
  //---------------------------------------------------
  analogWrite(inspeed, 175); //  speed
  // check to see if it's time to change the state 
  //---------------------------------------------------
  unsigned long currentMillis = millis();
  // DC motor update
  //---------------------------------------------------
  if((in1state == HIGH) && (currentMillis - previousMillis >= potvalue))
  {
    in1state = LOW;  // Turn it off
    previousMillis = currentMillis;  // Remember the time
    
    digitalWrite(in1, in1state);  // Update the actual values
    digitalWrite(in2, HIGH);  // Update the actual values
    digitalWrite(red, HIGH);  // red on
    digitalWrite(yellow, LOW);  // yellow off
  }
  else if ((in1state == LOW) && (currentMillis - previousMillis >= potvalue))
  {
    in1state = HIGH;  // turn it on
    previousMillis = currentMillis;   // Remember the time
    digitalWrite(in1, in1state);    // Update the actual values
    digitalWrite(in2, LOW);  // Update the actual values
    digitalWrite(red, LOW);  // red off
    digitalWrite(yellow, HIGH);  // yellow on
  }
    } else {
  unsigned long potvalue = map(analogRead(A0), 0, 1023, 60000 ,900000);
  
  display.clearDisplay();
  display.setTextSize(1.5);
  display.setTextColor(WHITE);
  display.setCursor(10,20);
  display.print("New round time OK");
  // update display with all of the above graphics
  display.display();
  delay(1000);        // delay in between reads for stability
    }
}
