# Fritzing sketch IR-schematic (saved by Fritzing 0.9.8b)
breadboards: 1

parts:
  Onderdeel1 = Arduino Uno (Rev3) - ICSP
  M1 = fc-51 [package=THT]

nets:
  N1: Onderdeel1.D3_PWM, M1.pin1
  N2: Onderdeel1.5V, M1.pin3
  N3: Onderdeel1.GND, M1.pin2
